# Fritzing sketch INA219_test_leds (saved by Fritzing 0.9.3b)
breadboards: 1

parts:
  Componente1 = INA219 High Side DC Current Sensor Breakout [part_number=904]
  YwRobot_Power_Supply1 = YwRobot Breadboard Power Supply [part_number=545043]
  Componente2 = Arduino Nano (Rev3.0) (ICSP)
  LCM1602_IIC1 = LCM1602 IIC [part_number="LCM1602 IIC" chip_label="LCM1602 IIC" package="DIP (Dual Inline) [THT]"]
  U1 = LCD-16X2 [package=lcd-16x2_noholes]
  R1 = Resistor [tolerance=±5% resistance=220 package=THT]
  R2 = Resistor [tolerance=±5% resistance=220 package=THT]
  LED1 = smd LED [color="Red (633nm)" package="1206 [SMD]"]
  LED2 = smd LED [color="Red (633nm)" package="1206 [SMD]"]

nets:
  N1: Componente1.VCC, Componente1.VIN+, YwRobot_Power_Supply1.VCC1
  N2: Componente1.GND, YwRobot_Power_Supply1.GND#11, YwRobot_Power_Supply1.GND#12
  N3: Componente1.SCL, Componente2.A5, LCM1602_IIC1.SCL
  N4: Componente1.SDA, Componente2.A4, LCM1602_IIC1.SDA
  5V: Componente1.VIN-, YwRobot_Power_Supply1.VCC2, Componente2.5V, LCM1602_IIC1.VCC
  GND: YwRobot_Power_Supply1.GND#13, YwRobot_Power_Supply1.GND#14, Componente2.GND, LCM1602_IIC1.GND, LED1.cathode, LED2.cathode
  N5: Componente2.D2, R2.Pin_1
  N6: Componente2.D3, R1.Pin_1
  VSS: LCM1602_IIC1.VSS, U1.VSS
  VDD: LCM1602_IIC1.VDD, U1.VDD
  N7: LCM1602_IIC1.V0, U1.VO
  N8: LCM1602_IIC1.RS, U1.RS
  N9: LCM1602_IIC1.RW, U1.R_W
  N10: LCM1602_IIC1.E, U1.E
  N11: LCM1602_IIC1.D0, U1.DB0
  N12: LCM1602_IIC1.D1, U1.DB1
  N13: LCM1602_IIC1.D2, U1.DB2
  N14: LCM1602_IIC1.D3, U1.DB3
  N15: LCM1602_IIC1.D4, U1.DB4
  N16: LCM1602_IIC1.D5, U1.DB5
  N17: LCM1602_IIC1.D6, U1.DB6
  N18: LCM1602_IIC1.D7, U1.DB7
  N19: LCM1602_IIC1.A, U1.A
  N20: LCM1602_IIC1.K, U1.K
  N21: R1.Pin_0, LED1.anode
  N22: R2.Pin_0, LED2.anode

custom parts:
  INA219 High Side DC Current Sensor Breakout: This breakout board will solve all your power-monitoring problems. Instead of struggling with two multimeters, you can just use the handy INA219B chip on this breakout to both measure both the high side voltage and DC current draw over I2C with 1% precision. Most current-measuring devices such as our current panel meter are only good for low side measuring. That means that unless you want to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
  YwRobot Breadboard Power Supply: The YwRobot Breadboard Power Supply (MB-V2) has two power rails; they can be 5V or 3V3. Power to the module can be provided through the female USB socket or through the A10 (female) 2.1mm power jack.
  LCM1602 IIC: I2C-Module to use a 1602 or 2004 LCD on with the wire.h libory Serial LCD Modul
